# Fritzing sketch phytotron (saved by Fritzing 0.9.4)
breadboards: 2

parts:
  U1 = ESP32S-30Pin [part_number=ESP32S-Generic]
  HC-SR04_Sensor_1 = HC-SR04 Ultrasonic Distance Sensor
  IIC2 = IIC Convterter [package=converter]
  LCD2 = LCD screen
  부품3 = FC-28 Soil Hygrometer Module - Probe
  부품4 = FC-28 Soil Hygrometer Module
  U2 = Module 4 Relais 5V [package="Module 4 Relais 5V"]
  Composant1 = Adafruit DS3231 [part_number="Adafruit #3013"]
  Part1 = KY-004 Key Switch Module [package="Breakout board"]
  Part2 = KY-004 Key Switch Module [package="Breakout board"]
  AM1 = AM2302 Humidity and Temperature Sensor
  Composant2 = Adafruit TSL2591 [part_number="Adafruit #1980"]

nets:
  N1: U1.EN, U1.GPIO32
  N2: U1.GPIO34, U1.GPIO21, Composant1.SCL, Composant2.SCL
  N3: U1.GPIO27, AM1.DATA
  GND: U1.GND, HC-SR04_Sensor_1.GND, 부품4.GND, Part1.Vin, Part2.Vin, AM1.GND, Composant2.GND
  N4: U1.GPIO22, Composant1.SDA, Composant2.SDA
  VCC: HC-SR04_Sensor_1.VCC, 부품4.VCC, Part1.-, Part2.-, AM1.VDD, Composant2.3.3V
  N5: IIC2.1, LCD2.VSS
  N6: IIC2.2, LCD2.VDD
  N7: IIC2.3, LCD2.V0
  N8: IIC2.4, LCD2.RS
  N9: IIC2.5, LCD2.R/W
  N10: IIC2.6, LCD2.E
  N11: IIC2.7, LCD2.DB0
  N12: IIC2.8, LCD2.DB1
  N13: IIC2.9, LCD2.DB2
  N14: IIC2.10, LCD2.DB3
  N15: IIC2.11, LCD2.DB4
  N16: IIC2.12, LCD2.DB5
  N17: IIC2.13, LCD2.DB6
  N18: IIC2.14, LCD2.DB7
  N19: IIC2.15, LCD2.LED+
  N20: IIC2.16, LCD2.LED-
  GND_2: IIC2.GND, U2.GND, Composant1.GND
  VCC_2: IIC2.Vcc, U2.VCC, Composant1.Vin
  N21: 부품3.POS, 부품4.POS
  N22: 부품3.NEG, 부품4.NEG
  N23: U2.JD-VCC, U2.VCC2

custom parts:
  ESP32S-30Pin: ESP-WROOM-32 ESP32 ESP-32S Development Board 2.4GHz Dual-Mode WiFi + Bluetooth Dual Cores Microcontroller The ESP32 integrated with Antenna switches, RF Balun, power amplifiers, low-noise amplifiers, filters, and management modules, and the entire solution occupies the least area of PCB. 2.4 GHz Wi-Fi plus Bluetooth dual-mode chip, with TSMC Ultra-low power consumption 40nm technology, power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
  IIC Convterter: Parallel to IIC Converter for HD44780 family LCDs
  FC-28 Soil Hygrometer Module - Probe: The FC-28 is a soil hygrometer module that uses the Texas Instruments LM393 comparator chip to provide an analog measurement of soil humidity.
  FC-28 Soil Hygrometer Module: The FC-28 is a soil hygrometer module that uses the Texas Instruments LM393 comparator chip to provide an analog measurement of soil humidity. The digital output is high when soil moisture is over a certain threshold, as determined by adjusting the potentiometer.
  Module 4 Relais 5V: Module 4 Relais 5V 4x SPD-06VDC-SD-C
  Adafruit DS3231: The datasheet for the DS3231 explains that this part is an "Extremely Accurate I²C-Integrated RTC/TCXO/Crystal". And, hey, it does exactly what it says on the tin! This Real Time Clock (RTC) is the most precise you can get in a small, low power package. Most RTCs use an external 32kHz timing crystal that is used to keep time with low current draw. And that's all well and good, but those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
  KY-004 Key Switch Module: Arduino Key Switch Module Keyes KY-004 is a push button that will output a high signal when pressed.
  Adafruit TSL2591: When the future is dazzlingly-bright, this ultra-high-range luminosity sensor will help you measure it. The TSL2591 luminosity sensor is an advanced digital light sensor, ideal for use in a wide range of light situations. Compared to low cost CdS cells, this sensor is more precise, allowing for exact lux calculations and can be configured for different gain/timing ranges to detect light ranges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
